# Fritzing sketch cd4060-timer (saved by Fritzing 0.9.3b)
breadboards: 1

parts:
  IC1 = IC, DIP package, 16 pins [chip_label=CD4060]
  Y1 = CRYSTAL [part_number=32KHz package=crystal-32khz-smd_epson_mc146]
  J1 = female pin header, 1 pin [form="♀ (female)"]
  Power_plug1 = Power plug
  R1 = Resistor [tolerance=±5% resistance=10M package=THT]
  R2 = Resistor [tolerance=±5% resistance=220k package=THT]
  C1 = Ceramic Capacitor [capacitance=15pF package="100 mil [THT, multilayer]"]
  C2 = Ceramic Capacitor [capacitance=33pF package="100 mil [THT, multilayer]"]

nets:
  N1: IC1.pin3, J1.pin1
  GND: IC1.pin8, IC1.pin12, Power_plug1.GND, C1.0, C2.1
  N2: IC1.pin10, R1.Pin_1, R2.Pin_1
  N3: IC1.pin11, Y1.1, R1.Pin_0, C1.1
  N4: IC1.pin16, Power_plug1.VCC
  N5: Y1.2, R2.Pin_0, C2.0
