# Fritzing sketch driver-pcb (saved by Fritzing 0.9.3b)
circuit board: 7cm x 5cm
breadboards: 1

parts:
  Q1 = Basic FET N-Channel [package="TO220 [THT]"]
  D1 = Rectifier Diode [part_number=1N4004 package="300 mil [THT]"]
  R1 = Resistor [tolerance=±5% resistance=470 package=THT]
  R2 = Resistor [tolerance=±5% resistance=10k package=THT]
  J1 = female pin header, 4 pins [form="♀ (female)"]
  J2 = female pin header, 6 pins [form="♀ (female)"]
  J3 = female pin header, 2 pins [form="♀ (female)"]
  D2 = Rectifier Diode [part_number=1N4001 package="300 mil [THT]"]
  R3 = Resistor [tolerance=±5% resistance=220 package=THT]
  R4 = Resistor [tolerance=±5% resistance=220 package=THT]
  R5 = Resistor [tolerance=±5% resistance=220 package=THT]
  R6 = Resistor [tolerance=±5% resistance=220 package=THT]
  D3 = Rectifier Diode [part_number=1N4001 package="300 mil [THT]"]
  Q3 = Basic FET N-Channel [package="TO220 [THT]"]
  Q4 = Basic FET N-Channel [package="TO220 [THT]"]
  D4 = Rectifier Diode [part_number=1N4001 package="300 mil [THT]"]

nets:
  N1: Q1.gate, R1.Pin_0, R2.Pin_0
  N2: Q1.drain, D1.anode, J2.pin1
  GND: Q1.source, R2.Pin_1, J1.pin4, J3.pin2, R4.Pin_1, R6.Pin_1, Q3.source, Q4.source
  N3: D1.cathode, J2.pin2, J2.pin4, J2.pin6, D2.cathode, D3.cathode, D4.cathode
  N4: R1.Pin_1, J1.pin1
  N5: J1.pin2, R3.Pin_1
  N6: J1.pin3, R5.Pin_1
  N7: J2.pin3, D2.anode, Q4.drain
  N8: J2.pin5, D3.anode, Q3.drain
  N9: J3.pin1, D4.anode
  N10: R3.Pin_0, R4.Pin_0, Q4.gate
  N11: R5.Pin_0, R6.Pin_0, Q3.gate

notes:
  12V
