# Fritzing sketch driver-pcb2 (saved by Fritzing 0.9.3b)
circuit board: 7cm x 5cm
breadboards: 1

parts:
  Q1 = Basic FET N-Channel [package="TO220 [THT]"]
  D1 = Rectifier Diode [part_number=1N4004 package="300 mil [THT]"]
  R1 = Resistor [tolerance=±5% resistance=470 package=THT]
  R2 = Resistor [tolerance=±5% resistance=10k package=THT]
  J1 = female pin header, 4 pins [form="♀ (female)"]
  J2 = female pin header, 6 pins [form="♀ (female)"]
  J3 = female pin header, 2 pins [form="♀ (female)"]
  D2 = Rectifier Diode [part_number=1N4001 package="300 mil [THT]"]
  R3 = Resistor [tolerance=±5% resistance=220 package=THT]
  R4 = Resistor [tolerance=±5% resistance=220 package=THT]
  R5 = Resistor [tolerance=±5% resistance=220 package=THT]
  R6 = Resistor [tolerance=±5% resistance=220 package=THT]
  D3 = Rectifier Diode [part_number=1N4001 package="300 mil [THT]"]
  Q3 = Basic FET N-Channel [package="TO220 [THT]"]
  Q4 = Basic FET N-Channel [package="TO220 [THT]"]
  D4 = Rectifier Diode [part_number=1N4001 package="300 mil [THT]"]
  S2 = 7 Segment Display
  S1 = 7 Segment Display
  J4 = female pin header, 5 pins [form="♀ (female)"]
  J5 = female pin header, 5 pins [form="♀ (female)"]
  R7 = Resistor [tolerance=±5% resistance=220 package=THT]
  Q5 = NPN-Transistor [package="TO92 [THT]"]
  Q6 = NPN-Transistor [package="TO92 [THT]"]
  R9 = Resistor [tolerance=±5% resistance=220 package=THT]
  R10 = Resistor [tolerance=±5% resistance=220 package=THT]
  R11 = Resistor [tolerance=±5% resistance=220 package=THT]
  R12 = Resistor [tolerance=±5% resistance=220 package=THT]
  R13 = Resistor [tolerance=±5% resistance=220 package=THT]
  R14 = Resistor [tolerance=±5% resistance=220 package=THT]
  R15 = Resistor [tolerance=±5% resistance=220 package=THT]
  R16 = Resistor [tolerance=±5% resistance=220 package=THT]
  R17 = Resistor [tolerance=±5% resistance=220 package=THT]

nets:
  N1: Q1.gate, R1.Pin_0, R2.Pin_0
  N2: Q1.drain, D1.anode, J2.pin1
  GND: Q1.source, R2.Pin_1, J1.pin4, J3.pin2, R4.Pin_1, R6.Pin_1, Q3.source, Q4.source, Q5.C, Q6.C
  N3: D1.cathode, J2.pin2, J2.pin4, J2.pin6, J3.pin1, D2.cathode, D3.cathode, D4.cathode
  N4: R1.Pin_1, J1.pin1
  N5: J1.pin2, R3.Pin_1
  N6: J1.pin3, R5.Pin_1
  N7: J2.pin3, D2.anode, Q4.drain
  N8: J2.pin5, D3.anode, Q3.drain
  N9: R3.Pin_0, R4.Pin_0, Q4.gate
  N10: R5.Pin_0, R6.Pin_0, Q3.gate
  N11: S2.Segment_E, S1.Segment_E, R15.Pin_0
  N12: S2.Segment_D, S1.Segment_D, R16.Pin_0
  N13: S2.Segment_C, S1.Segment_C, R17.Pin_0
  N14: S2.Segment_DP, S1.Segment_DP, R13.Pin_0
  N15: S2.Segment_B, S1.Segment_B, R12.Pin_1
  N16: S2.Segment_A, S1.Segment_A, R11.Pin_1
  N17: S2.common_cathode, Q6.E
  N18: S2.Segment_F, S1.Segment_F, R10.Pin_1
  N19: S2.Segment_G, S1.Segment_G, R7.Pin_1
  N20: S1.common_cathode, Q5.E
  N21: J4.pin1, R7.Pin_0
  N22: J4.pin2, R10.Pin_0
  N23: J4.pin3, R11.Pin_0
  N24: J4.pin4, R12.Pin_0
  N25: J4.pin5, R9.Pin_1
  N26: J5.pin1, R14.Pin_1
  N27: J5.pin2, R15.Pin_1
  N28: J5.pin3, R16.Pin_1
  N29: J5.pin4, R17.Pin_1
  N30: J5.pin5, R13.Pin_1
  N31: Q5.B, R9.Pin_0
  N32: Q6.B, R14.Pin_0

notes:
  12V
