# Fritzing sketch segment-driver (saved by Fritzing 0.9.3b)
breadboards: 1

parts:
  R4 = Resistor [tolerance=±5% resistance=470 package=THT]
  R5 = Resistor [tolerance=±5% resistance=470 package=THT]
  R6 = Resistor [tolerance=±5% resistance=470 package=THT]
  R7 = Resistor [tolerance=±5% resistance=470 package=THT]
  R8 = Resistor [tolerance=±5% resistance=470 package=THT]
  R2 = Resistor [tolerance=±5% resistance=470 package=THT]
  R1 = Resistor [tolerance=±5% resistance=470 package=THT]
  Digital_outputs_from_Arduino = female pin header, 8 pins [form="♀ (female)"]
  Q1 = NPN-Transistor [part_number=BC547 package="TO92 [THT]"]
  Q2 = NPN-Transistor [part_number=BC547 package="TO92 [THT]"]
  Digital_outputs_from_arduino = female pin header, 2 pins [form="♀ (female)"]
  Power_plug_(5V) = Power plug
  R3 = Resistor [tolerance=±5% resistance=470 package=THT]
  7_Segment1 = 7 Segment Display
  7_Segment2 = 7 Segment Display

nets:
  N1: R4.Pin_0, 7_Segment1.Segment_E, 7_Segment2.Segment_E
  N2: R4.Pin_1, Digital_outputs_from_Arduino.pin4
  N3: R5.Pin_0, 7_Segment1.Segment_D, 7_Segment2.Segment_D
  N4: R5.Pin_1, Digital_outputs_from_Arduino.pin5
  N5: R6.Pin_0, 7_Segment1.Segment_C, 7_Segment2.Segment_C
  N6: R6.Pin_1, Digital_outputs_from_Arduino.pin6
  N7: R7.Pin_0, 7_Segment1.Segment_B, 7_Segment2.Segment_B
  N8: R7.Pin_1, Digital_outputs_from_Arduino.pin7
  N9: R8.Pin_0, 7_Segment1.Segment_A, 7_Segment2.Segment_A
  N10: R8.Pin_1, Digital_outputs_from_Arduino.pin8
  N11: R2.Pin_0, 7_Segment1.Segment_G, 7_Segment2.Segment_G
  N12: R2.Pin_1, Digital_outputs_from_Arduino.pin2
  N13: R1.Pin_0, 7_Segment1.Segment_DP, 7_Segment2.Segment_DP
  N14: R1.Pin_1, Digital_outputs_from_Arduino.pin1
  N15: Digital_outputs_from_Arduino.pin3, R3.Pin_1
  GND: Q1.E, Q2.E, Power_plug_(5V).GND
  N16: Q1.B, Digital_outputs_from_arduino.pin1
  N17: Q1.C, 7_Segment1.common_cathode
  N18: Q2.B, Digital_outputs_from_arduino.pin2
  N19: Q2.C, 7_Segment2.common_cathode
  N20: R3.Pin_0, 7_Segment1.Segment_F, 7_Segment2.Segment_F
