# Fritzing sketch shield-1 (saved by Fritzing 0.9.3b)
circuit board: 8.46667cm x 5.64444cm
breadboards: 1

parts:
  J1 = female pin header, 8 pins [form="♀ (female)"]
  J2 = female pin header, 8 pins [form="♀ (female)"]
  J4 = female pin header, 6 pins [form="♀ (female)"]
  J5_(Vcc_5V) = female pin header, 5 pins [form="♀ (female)"]
  J6 = female pin header, 5 pins [form="♀ (female)"]
  IC1 = IC, DIP package, 16 pins [chip_label=IC]
  R1 = Resistor [tolerance=±5% resistance=220k package=THT]
  C1 = Ceramic Capacitor [capacitance=100nF package="100 mil [THT, multilayer]"]
  C2 = Ceramic Capacitor [capacitance=100nF package="100 mil [THT, multilayer]"]
  R2 = Resistor [tolerance=±5% resistance=10M package=THT]
  Onderdeel1 = Arduino Uno (Rev3)
  Y1 = CRYSTAL [package=tc26h]
  R3 = Resistor [tolerance=±5% resistance=4.7k package=THT]
  J7 = female pin header, 2 pins [form="♀ (female)"]
  R4 = Resistor [tolerance=±5% resistance=1k package=THT]
  R5 = Resistor [tolerance=±5% resistance=1k package=THT]
  R6 = Resistor [tolerance=±5% resistance=1k package=THT]

nets:
  N1: J1.pin1, Onderdeel1.D0/RX
  N2: J1.pin2, Onderdeel1.D1/TX
  N3: J1.pin3, Onderdeel1.D2
  N4: J1.pin4, Onderdeel1.D3_PWM
  N5: J1.pin5, Onderdeel1.D4
  N6: J1.pin6, Onderdeel1.D5_PWM
  N7: J1.pin7, Onderdeel1.D6_PWM
  N8: J1.pin8, Onderdeel1.D7
  N9: J2.pin1, Onderdeel1.D8
  N10: J2.pin2, Onderdeel1.D9_PWM
  N11: J2.pin3, Onderdeel1.D10_PWM/SS
  N12: J2.pin4, Onderdeel1.D11_PWM/MOSI
  N13: J2.pin5, Onderdeel1.D12/MISO
  N14: J2.pin6, Onderdeel1.D13/SCK
  GND: J2.pin7, J4.pin2, J4.pin3, J6.pin1, J6.pin2, J6.pin3, J6.pin4, J6.pin5, IC1.pin8, IC1.pin12, C1.1, C2.1, Onderdeel1.GND, J7.pin2, R4.Pin_0, R5.Pin_0, R6.Pin_0
  N15: J2.pin8, Onderdeel1.AREF
  N16: J4.pin1, Onderdeel1.VIN
  N17: J4.pin4, J5_(Vcc_5V).pin1, J5_(Vcc_5V).pin2, J5_(Vcc_5V).pin3, J5_(Vcc_5V).pin4, J5_(Vcc_5V).pin5, IC1.pin16, Onderdeel1.5V
  N18: J4.pin5, Onderdeel1.3V3
  N19: J4.pin6, Onderdeel1.RESET
  N20: IC1.pin3, Onderdeel1.A0, R3.Pin_0
  N21: IC1.pin10, R1.Pin_1, R2.Pin_0
  N22: IC1.pin11, C1.0, R2.Pin_1, Y1.2
  N23: R1.Pin_0, C2.0, Y1.1
  N24: Onderdeel1.A1, R4.Pin_1
  N25: Onderdeel1.A2, R5.Pin_1
  N26: Onderdeel1.A3, R6.Pin_1
  N27: R3.Pin_1, J7.pin1
