# Fritzing sketch shield-1a (saved by Fritzing 0.9.3b)
circuit board: 8.46667cm x 5.64444cm
breadboards: 1

parts:
  Onderdeel1 = Arduino Uno (Rev3)
  J1 = female pin header, 8 pins [form="♀ (female)"]
  J2 = female pin header, 8 pins [form="♀ (female)"]
  J3 = female pin header, 6 pins [form="♀ (female)"]
  J4 = female pin header, 6 pins [form="♀ (female)"]
  J5 = female pin header, 5 pins [form="♀ (female)"]
  J6 = female pin header, 5 pins [form="♀ (female)"]
  IC1 = IC, DIP package, 16 pins [chip_label=IC]

nets:
  N1: Onderdeel1.A0, J3.pin6
  N2: Onderdeel1.A1, J3.pin5
  N3: Onderdeel1.A2, J3.pin4
  N4: Onderdeel1.A3, J3.pin3
  N5: Onderdeel1.A4/SDA, J3.pin2
  N6: Onderdeel1.A5/SCL, J3.pin1
  N7: Onderdeel1.D8, J2.pin1
  N8: Onderdeel1.D9_PWM, J2.pin2
  N9: Onderdeel1.D10_PWM/SS, J2.pin3
  N10: Onderdeel1.D11_PWM/MOSI, J2.pin4
  N11: Onderdeel1.D12/MISO, J2.pin5
  N12: Onderdeel1.D13/SCK, J2.pin6
  N13: Onderdeel1.GND, J2.pin7, J4.pin2, J4.pin3, J6.pin1, J6.pin2, J6.pin3, J6.pin4, J6.pin5, IC1.pin8, IC1.pin12
  N14: Onderdeel1.AREF, J2.pin8
  N15: Onderdeel1.D0/RX, J1.pin1
  N16: Onderdeel1.D1/TX, J1.pin2
  N17: Onderdeel1.D2, J1.pin3
  N18: Onderdeel1.D3_PWM, J1.pin4
  N19: Onderdeel1.D4, J1.pin5
  N20: Onderdeel1.D5_PWM, J1.pin6
  N21: Onderdeel1.D6_PWM, J1.pin7
  N22: Onderdeel1.D7, J1.pin8
  N23: Onderdeel1.RESET, J4.pin6
  N24: Onderdeel1.3V3, J4.pin5
  N25: Onderdeel1.5V, J4.pin4, J5.pin1, J5.pin2, J5.pin3, J5.pin4, J5.pin5, IC1.pin16
  N26: Onderdeel1.VIN, J4.pin1
