# Fritzing sketch shield-2 (saved by Fritzing 0.9.3b)
circuit board: 7cm x 5cm
breadboards: 1

parts:
  J1 = female pin header, 8 pins [form="♀ (female)"]
  J2 = female pin header, 8 pins [form="♀ (female)"]
  J3 = female pin header, 6 pins [form="♀ (female)"]
  J6 = female pin header, 6 pins [form="♀ (female)"]
  R1 = Resistor [tolerance=±5% resistance=220 package=THT]
  R2 = Resistor [tolerance=±5% resistance=220 package=THT]
  Q1 = Basic FET P-Channel [part_number=IRL540N package="TO220 [THT]"]
  Q2 = Basic FET P-Channel [part_number=IRL540N package="TO220 [THT]"]
  Q3 = Basic FET P-Channel [part_number=IRL540N package="TO220 [THT]"]
  J7 = Camdenboss CTB0158-6 [part_number=CTB0158-6 package=THT]
  D1 = Rectifier Diode [part_number=1N4004 package="300 mil [THT]"]
  D2 = Rectifier Diode [part_number=1N4004 package="300 mil [THT]"]
  D3 = Rectifier Diode [part_number=1N4004 package="300 mil [THT]"]
  R3 = Resistor [tolerance=±5% resistance=1k package=THT]
  R4 = Resistor [tolerance=±5% resistance=1k package=THT]
  R5 = Resistor [tolerance=±5% resistance=1k package=THT]
  Q4 = NPN-Transistor [part_number=BCF547 package="TO92 [THT]"]
  Q5 = NPN-Transistor [part_number=BCF547 package="TO92 [THT]"]
  R6 = Resistor [tolerance=±5% resistance=470 package=THT]
  R7 = Resistor [tolerance=±5% resistance=470 package=THT]
  R8 = Resistor [tolerance=±5% resistance=220 package=THT]
  R9 = Resistor [tolerance=±5% resistance=220 package=THT]
  R10 = Resistor [tolerance=±5% resistance=220 package=THT]
  R11 = Resistor [tolerance=±5% resistance=220 package=THT]
  R12 = Resistor [tolerance=±5% resistance=220 package=THT]
  R13 = Resistor [tolerance=±5% resistance=220 package=THT]
  Power_plug1 = Power plug
  S1 = Pushbutton [package="[THT]"]
  S2 = Pushbutton [package="[THT]"]
  R14 = Resistor [tolerance=±5% resistance=4.7k package=THT]
  R15 = Resistor [tolerance=±5% resistance=4.7k package=THT]
  Digit_1 = 7 Segment Display
  Digit_2 = 7 Segment Display

nets:
  N1: J1.pin1, R12.Pin_0
  N2: J1.pin2, R13.Pin_0
  N3: J1.pin4, R10.Pin_0
  N4: J1.pin5, R11.Pin_0
  N5: J1.pin6, R1.Pin_0
  N6: J1.pin7, R9.Pin_0
  N7: J1.pin8, R8.Pin_0
  N8: J2.pin1, R2.Pin_0
  N9: J2.pin2, R6.Pin_0
  N10: J2.pin3, R7.Pin_0
  N11: J2.pin4, R5.Pin_0
  N12: J2.pin5, R4.Pin_0
  N13: J2.pin6, R3.Pin_0
  GND: J2.pin7, Q1.source, Q2.source, Q3.source, Q4.E, Q5.E, Power_plug1.GND
  N14: J3.pin5, R14.Pin_1
  N15: J3.pin6, R15.Pin_0
  N16: J6.pin4, S1.Pin_3, S1.Pin_4, S2.Pin_3, S2.Pin_4
  N17: R1.Pin_1, Digit_1.Segment_E, Digit_2.Segment_E
  N18: R2.Pin_1, Digit_1.Segment_B, Digit_2.Segment_B
  N19: Q1.gate, R5.Pin_1
  N20: Q1.drain, J7.pin1, D3.anode
  N21: Q2.gate, R4.Pin_1
  N22: Q2.drain, J7.pin3, D2.anode
  N23: Q3.gate, R3.Pin_1
  N24: Q3.drain, J7.pin5, D1.anode
  N25: J7.pin2, J7.pin4, J7.pin6, D1.cathode, D2.cathode, D3.cathode, Power_plug1.VCC
  N26: Q4.B, R6.Pin_1
  N27: Q4.C, Digit_2.common_cathode
  N28: Q5.B, R7.Pin_1
  N29: Q5.C, Digit_1.common_cathode
  N30: R8.Pin_1, Digit_1.Segment_A, Digit_2.Segment_A
  N31: R9.Pin_1, Digit_1.Segment_D, Digit_2.Segment_D
  N32: R10.Pin_1, Digit_1.Segment_C, Digit_2.Segment_C
  N33: R11.Pin_1, Digit_1.Segment_DP, Digit_2.Segment_DP
  N34: R12.Pin_1, Digit_1.Segment_G, Digit_2.Segment_G
  N35: R13.Pin_1, Digit_1.Segment_F, Digit_2.Segment_F
  N36: S1.Pin_1, S1.Pin_2, R15.Pin_1
  N37: S2.Pin_1, S2.Pin_2, R14.Pin_0

notes:
  12V
  5V
  Solenoid 1
  Solenoid 2
  Solenoid 3
  A4 (switch 2)
  A5 (switch 1)
  0 (segment G)
  7 (segment A)
  8 (segment B)
  9 (digit 2)
  10 (digit 1)
  11 (trigger solenoid 1)
  12 (trigger solenoid 2)
  13 (trigger solenoid 3)
  GND
  1 (segment F)
  4 (segment DP)
  3 (segment C)
  5 (segment E)
  6 (segment D)
