# Fritzing sketch solenoid-driver (saved by Fritzing 0.9.3b)
breadboards: 1

parts:
  Power_plug_(12V) = Power plug
  Q1 = Basic FET N-Channel [part_number=IRL540N package="TO220 [THT]"]
  Digital_out_from_Arduino = female pin header, 1 pin [form="♀ (female)"]
  D1 = Rectifier Diode [part_number=1N4004 package="300 mil [THT]"]
  Solenoid_connection = Camdenboss CTB0158-2 [part_number=CTB0158-2 package=THT]
  C1 = Electrolytic Capacitor [capacitance=2.2mF package="100 mil [THT, electrolytic]"]
  R1 = Resistor [tolerance=±5% resistance=470 package=THT]
  R2 = Resistor [tolerance=±5% resistance=10k package=THT]

nets:
  GND: Power_plug_(12V).GND, Q1.source, C1.-, R2.Pin_1
  N1: Power_plug_(12V).VCC, D1.cathode, Solenoid_connection.pin2, C1.+
  N2: Q1.gate, R1.Pin_1, R2.Pin_0
  N3: Q1.drain, D1.anode, Solenoid_connection.pin1
  N4: Digital_out_from_Arduino.pin1, R1.Pin_0
